// Logisim project smips.circ as structural Verilog
module Board (
);

  wire CLK, HALT, MEM_WE, RESET, TTY_WE;
  wire [3:0] MEM_BE;
  wire [6:0] TTY_DATA;
  wire [31:0] MEM_ADDR, MEM_RDATA, MEM_WDATA;

  Clock Reloj (.out(CLK));
  Button u_Reset (.out(RESET));
  CPU cpu_1 (
    .CLK(CLK), .RESET(RESET), .MEM_RDATA(MEM_RDATA), .MEM_ADDR(MEM_ADDR), .MEM_WDATA(MEM_WDATA),
    .MEM_BE(MEM_BE), .MEM_WE(MEM_WE), .TTY_DATA(TTY_DATA), .TTY_WE(TTY_WE), .HALT(HALT));
  TTY #(.cols(48), .rows(12)) tty_1 (.data(TTY_DATA), .clk(CLK), .we(TTY_WE), .clr(RESET));
  Memory memory_1 (.CLK(CLK), .ADDR(MEM_ADDR), .WDATA(MEM_WDATA), .BE(MEM_BE), .WE(MEM_WE), .RDATA(MEM_RDATA));
  LED u_Halt (.in(HALT));

  // Notes on the sheet:
  //   S-MIPS | Board
  //   No modificar: la CPU se implementa dentro del subcircuito CPU.
endmodule

module CPU (
  input  CLK,
  input  RESET,
  input  [31:0] MEM_RDATA,
  output [31:0] MEM_ADDR,
  output [31:0] MEM_WDATA,
  output [3:0] MEM_BE,
  output MEM_WE,
  output [6:0] TTY_DATA,
  output TTY_WE,
  output HALT
);

  Instruction_Decoder instruction_decoder_1 ();  // open: Funct, Op, IMM_MODE, ALU_OP, Is_Syscall, Is_Load, Is_Store, Is_Branch, Is_Jump
  Datapath datapath_1 ();  // open: ALU_OP, in_2, Shamt, ALUSrcA_SEL, ALUSrcB_SEL, WRITE_BACK, in_7, in_8, in_9, MEM_RDATA, RegWrite, PC_OUT, MEM_WDATA, MEM_ADDR, MEM_BE, BR_EQ
  Branch_Control branch_control_1 ();  // open: Bne, Op1, Beq, Op2, Branch_Taken

  // Notes on the sheet:
  //   CPU S-MIPS: implementar aqui
  //   No cambiar nombres, anchos ni sentido de los pines: la placa depende de ellos.
endmodule

module Memory (
  input  CLK,
  input  [31:0] ADDR,
  input  [31:0] WDATA,
  input  [3:0] BE,
  input  WE,
  output [31:0] RDATA
);

  RAM #(.addrWidth(12), .asyncread("true"), .byteenables("byteEnables"), .dataWidth(32), .\type ("nonvolatile")) Main_Memory (
    .addr(ADDR[13:2]), .we(WE), .oe(1'b1), .clk(CLK), .din(WDATA), .dout(RDATA), .be3(BE[3]), .be2(BE[2]),
    .be1(BE[1]), .be0(BE[0]));

  // Other names for the same wires on the sheet: A[11:0] = ADDR[13:2]

  // Notes on the sheet:
  //   Memoria unificada: 4096 palabras de 32 bits (16 KiB), little-endian
  //   Lectura combinacional; escritura en el flanco de subida de CLK con WE=1, solo en los bytes con BE=1.
  //   Se usan los bits 13..2 de ADDR; los demas se ignoran (el espacio se repite cada 16 KiB).
endmodule

module Datapath (
  input  [2:0] ALU_OP,
  input  in_2,
  input  [4:0] Shamt,
  input  [1:0] ALUSrcA_SEL,
  input  [1:0] ALUSrcB_SEL,
  input  [31:0] WRITE_BACK,
  input  in_7,
  input  in_8,
  input  in_9,
  input  [31:0] MEM_RDATA,
  input  RegWrite,
  output [31:0] PC_OUT,
  output [31:0] MEM_WDATA,
  output [31:0] MEM_ADDR,
  output [3:0] MEM_BE,
  output BR_EQ
);

  wire CLK;
  wire [1:0] undriven_3;
  wire [15:0] Imm16;
  wire [31:0] A_q, alu_1_result, ALUOUT, B_q, bit_extender_1_out, bit_extender_2_out, IR_OUT, MDROUT,
       multiplexer_1_out, multiplexer_3_out, multiplexer_4_out, undriven, undriven_2;

  Clock clock_1 (.out(CLK));
  Register #(.width(32)) IR (.en(in_8), .clk(CLK), .Q(IR_OUT), .clr(in_2));  // open: D
  Register #(.width(32)) MDR (.D(MEM_RDATA), .clk(CLK), .Q(MDROUT));  // open: en, clr
  Register_File register_file_1 ();  // open: in_1, in_2, in_3, in_4, in_5, in_6, out_7, out_8
  Register #(.width(32)) A (.D(undriven_2), .en(1'b1), .clk(CLK), .Q(A_q));  // open: clr
  Register #(.width(32)) B (.D(undriven), .en(1'b1), .clk(CLK), .Q(B_q));  // open: clr
  Multiplexer #(.select(2), .width(32)) multiplexer_1 (
    .in3(ALUOUT), .out(multiplexer_1_out), .sel(undriven_3));  // open: in0, in1, in2
  Register #(.width(32)) PC (.D(multiplexer_1_out), .en(in_9), .clk(CLK), .Q(PC_OUT), .clr(in_2));
  Multiplexer #(.width(32)) multiplexer_2 (.in0(ALUOUT), .in1(MDROUT), .out(WRITE_BACK));  // open: sel
  assign bit_extender_1_out = {{27{Shamt[4]}}, Shamt};  // Bit_Extender bit_extender_1
  assign bit_extender_2_out = {{16{Imm16[15]}}, Imm16};  // Bit_Extender bit_extender_2
  Bit_Extender #(.in_width(16), .out_width(32), .\type ("zero")) bit_extender_3 (.in(Imm16));  // open: out
  Multiplexer #(.select(2), .width(32)) multiplexer_3 (
    .in0(PC_OUT), .in1(A_q), .in2(bit_extender_1_out), .out(multiplexer_3_out), .sel(ALUSrcA_SEL));  // open: in3
  Multiplexer #(.select(2), .width(32)) multiplexer_4 (
    .in0(B_q), .in1(32'h4), .in2(bit_extender_2_out), .out(multiplexer_4_out), .sel(ALUSrcB_SEL));  // open: in3
  Shifter #(.width(32)) shifter_1 (.in(bit_extender_2_out), .\dist (5'b00010));  // open: out
  ALU alu_1 (.A(multiplexer_3_out), .B(multiplexer_4_out), .ALU_OP(ALU_OP), .RESULT(alu_1_result), .ZERO_F(in_7));
  Register #(.width(32)) u_ALUOUT (.D(alu_1_result), .clk(CLK), .Q(ALUOUT));  // open: en, clr

  // Other names for the same wires on the sheet: IRWrite = in_8; PCWrite = in_9; RESET = in_2; ZERO = in_7

  // Notes on the sheet:
  //   ALUSrcA
  //   ALUSrcB
  //   INPUTS/OUTPUTS
endmodule

module Instruction_Decoder (
  input  [5:0] Funct,
  input  [5:0] Op,
  output [1:0] IMM_MODE,
  output [2:0] ALU_OP,
  output Is_Syscall,
  output Is_Load,
  output Is_Store,
  output Is_Branch,
  output Is_Jump
);

  wire comparator_1_eq, comparator_2_eq, comparator_3_eq, comparator_4_eq, comparator_5_eq, comparator_6_eq,
       comparator_7_eq, comparator_8_eq, comparator_9_eq, comparator_10_eq, comparator_11_eq,
       comparator_12_eq, comparator_13_eq, comparator_14_eq, comparator_15_eq, comparator_16_eq,
       comparator_18_eq, comparator_19_eq, comparator_22_eq, comparator_23_eq, comparator_25_eq, I_ADD,
       I_AND, I_LUI, I_OR, I_SLT, I_VALID, ILLEGAL, OP_ZERO, or_5_out, R_ADD, R_AND, R_JR, R_OR, R_SLL,
       R_SLT, R_SRL, R_SUB, R_VALID, VALID_INS;

  Comparator #(.width(6)) comparator_1 (.a(Funct), .b(6'b001100), .eq(comparator_1_eq));  // open: gt, lt
  Comparator #(.width(6)) comparator_2 (.a(Op), .b(6'b100011), .eq(comparator_2_eq));  // open: gt, lt
  Comparator #(.width(6)) comparator_3 (.a(Op), .b(6'b100000), .eq(comparator_3_eq));  // open: gt, lt
  Comparator #(.width(6)) comparator_4 (.a(Op), .b(6'b100100), .eq(comparator_4_eq));  // open: gt, lt
  Comparator #(.width(6)) comparator_5 (.a(Op), .b(6'b101011), .eq(comparator_5_eq));  // open: gt, lt
  Comparator #(.width(6)) comparator_6 (.a(Op), .b(6'b101000), .eq(comparator_6_eq));  // open: gt, lt
  Comparator #(.width(6)) comparator_7 (.a(Op), .b(6'b000100), .eq(comparator_7_eq));  // open: gt, lt
  Comparator #(.width(6)) comparator_8 (.a(Op), .b(6'b000101), .eq(comparator_8_eq));  // open: gt, lt
  Comparator #(.width(6)) comparator_9 (.a(Op), .b(6'b000010), .eq(comparator_9_eq));  // open: gt, lt
  Comparator #(.width(6)) comparator_10 (.a(Op), .b(6'b000011), .eq(comparator_10_eq));  // open: gt, lt
  nor nor_1 (OP_ZERO, Op[0], Op[1], Op[2], Op[4], Op[5]);
  and and_1 (Is_Syscall, comparator_1_eq, OP_ZERO);
  or or_1 (Is_Store, comparator_5_eq, comparator_6_eq);
  or or_2 (Is_Branch, comparator_7_eq, comparator_8_eq);
  or or_3 (Is_Jump, comparator_9_eq, comparator_10_eq);
  or or_4 (Is_Load, comparator_2_eq, comparator_3_eq, comparator_4_eq);
  Comparator #(.width(6)) comparator_11 (.a(Funct), .b(6'b100000), .eq(comparator_11_eq));  // open: gt, lt
  Comparator #(.width(6)) comparator_12 (.a(Funct), .b(6'b001100), .eq(comparator_12_eq));  // open: gt, lt
  Comparator #(.width(6)) comparator_13 (.a(Funct), .b(6'b100010), .eq(comparator_13_eq));  // open: gt, lt
  Comparator #(.width(6)) comparator_14 (.a(Funct), .b(6'b100100), .eq(comparator_14_eq));  // open: gt, lt
  Comparator #(.width(6)) comparator_15 (.a(Funct), .b({6{1'b0}}), .eq(comparator_15_eq));  // open: gt, lt
  Comparator #(.width(6)) comparator_16 (.a(Funct), .b(6'b000010), .eq(comparator_16_eq));  // open: gt, lt
  Comparator #(.width(6)) comparator_17 (.a(Op), .b(6'b001100), .eq(I_AND));  // open: gt, lt
  or or_5 (or_5_out, comparator_11_eq, comparator_12_eq);
  Comparator #(.width(6)) comparator_18 (.a(Funct), .b(6'b100101), .eq(comparator_18_eq));  // open: gt, lt
  Comparator #(.width(6)) comparator_19 (.a(Funct), .b(6'b101010), .eq(comparator_19_eq));  // open: gt, lt
  and and_2 (R_SLL, comparator_15_eq, OP_ZERO);
  and and_3 (R_SRL, comparator_16_eq, OP_ZERO);
  and and_4 (R_ADD, or_5_out, OP_ZERO);
  and and_5 (R_SUB, comparator_13_eq, OP_ZERO);
  and and_6 (R_AND, comparator_14_eq, OP_ZERO);
  and and_7 (R_OR, comparator_18_eq, OP_ZERO);
  and and_8 (R_SLT, comparator_19_eq, OP_ZERO);
  Comparator #(.width(6)) comparator_20 (.a(Op), .b(6'b001101), .eq(I_OR));  // open: gt, lt
  Comparator #(.width(6)) comparator_21 (.a(Op), .b(6'b001010), .eq(I_SLT));  // open: gt, lt
  Comparator #(.width(6)) comparator_22 (.a(Op), .b(6'b001000), .eq(comparator_22_eq));  // open: gt, lt
  Comparator #(.width(6)) comparator_23 (.a(Op), .b(6'b001001), .eq(comparator_23_eq));  // open: gt, lt
  or or_6 (I_ADD, comparator_22_eq, comparator_23_eq);
  or or_7 (ALU_OP[0], I_OR, R_OR, R_SUB, Is_Branch, R_SLL);
  or or_8 (ALU_OP[1], R_AND, R_OR, I_AND, I_OR, R_SRL);
  or or_9 (ALU_OP[2], I_SLT, R_SRL, R_SLT, R_SLL);
  Comparator #(.width(6)) comparator_24 (.a(Op), .b(6'b001111), .eq(I_LUI));  // open: gt, lt
  Comparator #(.width(6)) comparator_25 (.a(Funct), .b(6'b001000), .eq(comparator_25_eq));  // open: gt, lt
  and and_9 (R_JR, comparator_25_eq, OP_ZERO);
  or or_10 (R_VALID, R_SRL, R_SLL, R_SLT, R_SUB, R_OR, R_JR, R_AND, R_ADD);
  or or_11 (I_VALID, Is_Store, Is_Load, I_SLT, I_OR, I_LUI, I_AND, I_ADD);
  or or_12 (VALID_INS, Is_Syscall, R_VALID, I_VALID, Is_Branch, Is_Jump);
  not not_1 (ILLEGAL, VALID_INS);

  // Other names for the same wires on the sheet: ALU_OP_0 = ALU_OP[0]; ALU_OP_1 = ALU_OP[1]; ALU_OP_2 = ALU_OP[2];
  //   IMM_ZERO = IMM_MODE[0]; IMM_LUI = IMM_MODE[1]
endmodule

module Branch_Control (
  input  Bne,
  input  [31:0] Op1,
  input  Beq,
  input  [31:0] Op2,
  output Branch_Taken
);

  wire and_1_out, and_2_out, comparator_1_eq, not_1_out;

  Comparator #(.width(32)) comparator_1 (.a(Op1), .b(Op2), .eq(comparator_1_eq));  // open: gt, lt
  not not_1 (not_1_out, comparator_1_eq);
  and and_1 (and_1_out, comparator_1_eq, Beq);
  and and_2 (and_2_out, Bne, not_1_out);
  or or_1 (Branch_Taken, and_2_out, and_1_out);
endmodule

module Register_File (
  input  in_1,
  input  in_2,
  input  [4:0] in_3,
  input  [4:0] in_4,
  input  [4:0] in_5,
  input  [31:0] in_6,
  output [31:0] out_7,
  output [31:0] out_8
);

  wire CLK, decoder_1_out0, decoder_1_out1, decoder_1_out2, decoder_1_out3, decoder_1_out4, decoder_1_out5,
       decoder_1_out6, decoder_1_out7, decoder_1_out8, decoder_1_out9, decoder_1_out10, decoder_1_out11,
       decoder_1_out12, decoder_1_out13, decoder_1_out14, decoder_1_out15, decoder_1_out16, decoder_1_out17,
       decoder_1_out18, decoder_1_out19, decoder_1_out20, decoder_1_out21, decoder_1_out22, decoder_1_out23,
       decoder_1_out24, decoder_1_out25, decoder_1_out26, decoder_1_out27, decoder_1_out28, decoder_1_out29,
       decoder_1_out30, decoder_1_out31, R1, R2, R3, R4, R5, R6, R7, R8, R9, R10, R11, R12, R13, R14, R15,
       R16, R17, R18, R19, R20, R21, R22, R23, R24, R25, R26, R27, R28, R29, R30, R31, R32;
  wire [31:0] R1O, R2O, R3O, R4O, R5O, R6O, R7O, R8O, R9O, R10O, R11O, R12O, R13O, R14O, R15O, R16O, R17O,
       R18O, R19O, R20O, R21O, R22O, R23O, R24O, R25O, R26O, R27O, R28O, R29O, R30O, R31O, R32O;

  Clock clock_1 (.out(CLK));
  Register #(.width(32)) u_R1 (.D(in_6), .en(R1), .clk(CLK), .Q(R1O), .clr(in_1));
  Register #(.width(32)) u_R5 (.D(in_6), .en(R5), .clk(CLK), .Q(R5O), .clr(in_1));
  Register #(.width(32)) u_R9 (.D(in_6), .en(R9), .clk(CLK), .Q(R9O), .clr(in_1));
  Register #(.width(32)) u_R13 (.D(in_6), .en(R13), .clk(CLK), .Q(R13O), .clr(in_1));
  Register #(.width(32)) u_R17 (.D(in_6), .en(R17), .clk(CLK), .Q(R17O), .clr(in_1));
  Register #(.width(32)) u_R21 (.D(in_6), .en(R21), .clk(CLK), .Q(R21O), .clr(in_1));
  Register #(.width(32)) u_R25O (.D(in_6), .en(R25), .clk(CLK), .Q(R25O), .clr(in_1));
  Register #(.width(32)) u_R29 (.D(in_6), .en(R29), .clk(CLK), .Q(R29O), .clr(in_1));
  Register #(.width(32)) u_R2 (.D(in_6), .en(R2), .clk(CLK), .Q(R2O), .clr(in_1));
  Register #(.width(32)) u_R6 (.D(in_6), .en(R6), .clk(CLK), .Q(R6O), .clr(in_1));
  Register #(.width(32)) u_R10 (.D(in_6), .en(R10), .clk(CLK), .Q(R10O), .clr(in_1));
  Register #(.width(32)) u_R14 (.D(in_6), .en(R14), .clk(CLK), .Q(R14O), .clr(in_1));
  Register #(.width(32)) u_R18 (.D(in_6), .en(R18), .clk(CLK), .Q(R18O), .clr(in_1));
  Register #(.width(32)) u_R22 (.D(in_6), .en(R22), .clk(CLK), .Q(R22O), .clr(in_1));
  Register #(.width(32)) u_R26O (.D(in_6), .en(R26), .clk(CLK), .Q(R26O), .clr(in_1));
  Register #(.width(32)) u_R30 (.D(in_6), .en(R30), .clk(CLK), .Q(R30O), .clr(in_1));
  Register #(.width(32)) u_R3 (.D(in_6), .en(R3), .clk(CLK), .Q(R3O), .clr(in_1));
  Register #(.width(32)) u_R7 (.D(in_6), .en(R7), .clk(CLK), .Q(R7O), .clr(in_1));
  Register #(.width(32)) u_R11 (.D(in_6), .en(R11), .clk(CLK), .Q(R11O), .clr(in_1));
  Register #(.width(32)) u_R15 (.D(in_6), .en(R15), .clk(CLK), .Q(R15O), .clr(in_1));
  Register #(.width(32)) u_R19 (.D(in_6), .en(R19), .clk(CLK), .Q(R19O), .clr(in_1));
  Register #(.width(32)) u_R23 (.D(in_6), .en(R23), .clk(CLK), .Q(R23O), .clr(in_1));
  Register #(.width(32)) u_R27 (.D(in_6), .en(R27), .clk(CLK), .Q(R27O), .clr(in_1));
  Register #(.width(32)) u_R31 (.D(in_6), .en(R31), .clk(CLK), .Q(R31O), .clr(in_1));
  Register #(.width(32)) u_R4 (.D(in_6), .en(R4), .clk(CLK), .Q(R4O), .clr(in_1));
  Register #(.width(32)) u_R8 (.D(in_6), .en(R8), .clk(CLK), .Q(R8O), .clr(in_1));
  Register #(.width(32)) u_R12 (.D(in_6), .en(R12), .clk(CLK), .Q(R12O), .clr(in_1));
  Register #(.width(32)) u_R16 (.D(in_6), .en(R16), .clk(CLK), .Q(R16O), .clr(in_1));
  Register #(.width(32)) u_R20 (.D(in_6), .en(R20), .clk(CLK), .Q(R20O), .clr(in_1));
  Register #(.width(32)) u_R24 (.D(in_6), .en(R24), .clk(CLK), .Q(R24O), .clr(in_1));
  Register #(.width(32)) u_R28 (.D(in_6), .en(R28), .clk(CLK), .Q(R28O), .clr(in_1));
  Register #(.width(32)) u_R32 (.D(in_6), .en(R32), .clk(CLK), .Q(R32O));  // open: clr
  Decoder #(.select(5)) decoder_1 (
    .out0(decoder_1_out0), .out1(decoder_1_out1), .out2(decoder_1_out2), .out3(decoder_1_out3),
    .out4(decoder_1_out4), .out5(decoder_1_out5), .out6(decoder_1_out6), .out7(decoder_1_out7),
    .out8(decoder_1_out8), .out9(decoder_1_out9), .out10(decoder_1_out10), .out11(decoder_1_out11),
    .out12(decoder_1_out12), .out13(decoder_1_out13), .out14(decoder_1_out14), .out15(decoder_1_out15),
    .out16(decoder_1_out16), .out17(decoder_1_out17), .out18(decoder_1_out18), .out19(decoder_1_out19),
    .out20(decoder_1_out20), .out21(decoder_1_out21), .out22(decoder_1_out22), .out23(decoder_1_out23),
    .out24(decoder_1_out24), .out25(decoder_1_out25), .out26(decoder_1_out26), .out27(decoder_1_out27),
    .out28(decoder_1_out28), .out29(decoder_1_out29), .out30(decoder_1_out30), .out31(decoder_1_out31),
    .sel(in_5));  // open: en
  and and_1 (R1, in_2, decoder_1_out0);
  and and_2 (R2, in_2, decoder_1_out1);
  and and_3 (R32, in_2, decoder_1_out31);
  and and_4 (R31, in_2, decoder_1_out30);
  and and_5 (R3, in_2, decoder_1_out2);
  and and_6 (R4, in_2, decoder_1_out3);
  and and_7 (R30, in_2, decoder_1_out29);
  and and_8 (R29, in_2, decoder_1_out28);
  and and_9 (R5, in_2, decoder_1_out4);
  and and_10 (R6, in_2, decoder_1_out5);
  and and_11 (R28, in_2, decoder_1_out27);
  and and_12 (R27, in_2, decoder_1_out26);
  and and_13 (R7, in_2, decoder_1_out6);
  and and_14 (R8, in_2, decoder_1_out7);
  and and_15 (R26, in_2, decoder_1_out25);
  and and_16 (R25, in_2, decoder_1_out24);
  Multiplexer #(.select(5), .width(32)) multiplexer_1 (
    .in0(R1O), .in1(R2O), .in2(R3O), .in3(R4O), .in4(R5O), .in5(R6O), .in6(R7O), .in7(R8O), .in8(R9O),
    .in9(R10O), .in10(R11O), .in11(R12O), .in12(R13O), .in13(R14O), .in14(R15O), .in15(R16O), .in16(R17O),
    .in17(R18O), .in18(R19O), .in19(R20O), .in20(R21O), .in21(R22O), .in22(R23O), .in23(R24O), .in24(R25O),
    .in25(R26O), .in26(R27O), .in27(R28O), .in28(R29O), .in29(R30O), .in30(R31O), .in31(R32O), .out(out_7),
    .sel(in_3));
  Multiplexer #(.select(5), .width(32)) multiplexer_2 (
    .in0(R1O), .in1(R2O), .in2(R3O), .in3(R4O), .in4(R5O), .in5(R6O), .in6(R7O), .in7(R8O), .in8(R9O),
    .in9(R10O), .in10(R11O), .in11(R12O), .in12(R13O), .in13(R14O), .in14(R15O), .in15(R16O), .in16(R17O),
    .in17(R18O), .in18(R19O), .in19(R20O), .in20(R21O), .in21(R22O), .in22(R23O), .in23(R24O), .in24(R25O),
    .in25(R26O), .in26(R27O), .in27(R28O), .in28(R29O), .in29(R30O), .in30(R31O), .in31(R32O), .out(out_8),
    .sel(in_4));
  and and_17 (R9, in_2, decoder_1_out8);
  and and_18 (R10, in_2, decoder_1_out9);
  and and_19 (R24, in_2, decoder_1_out23);
  and and_20 (R23, in_2, decoder_1_out22);
  and and_21 (R11, in_2, decoder_1_out10);
  and and_22 (R12, in_2, decoder_1_out11);
  and and_23 (R22, in_2, decoder_1_out21);
  and and_24 (R21, in_2, decoder_1_out20);
  and and_25 (R13, in_2, decoder_1_out12);
  and and_26 (R14, in_2, decoder_1_out13);
  and and_27 (R20, in_2, decoder_1_out19);
  and and_28 (R19, in_2, decoder_1_out18);
  and and_29 (R15, in_2, decoder_1_out14);
  and and_30 (R16, in_2, decoder_1_out15);
  and and_31 (R18, in_2, decoder_1_out17);
  and and_32 (R17, in_2, decoder_1_out16);

  // Other names for the same wires on the sheet: READ_DATA1[31:0] = out_7; READ_DATA2[31:0] = out_8; Reg_wr = in_2;
  //   RESET = in_1; Rs[4:0] = in_3; Rt[4:0] = in_4; Wa_wr[4:0] = in_5; Wd[31:0] = in_6

  // Notes on the sheet:
  //   INPUTS
  //   OUTPUTS
  //   REGISTER_BANK
  //   REGISTER SELECTOR
  //   OUTPUT SELECTOR
endmodule

module ALU (
  input  [31:0] A,
  input  [31:0] B,
  input  [2:0] ALU_OP,
  output [31:0] RESULT,
  output ZERO_F
);

  wire CLK, comparator_1_lt;
  wire [31:0] ADD, ALU_AND, ALU_OR, Comp_sig, L_LEFT, L_RIGHT, REST;

  Adder #(.width(32)) adder_1 (.a(A), .b(B), .out(ADD));  // open: cin, cout
  Subtractor #(.width(32)) subtractor_1 (.a(A), .b(B), .out(REST));  // open: bin, bout
  assign ADD = A & B;  // AND_Gate and_1, 32 bits wide
  assign ALU_OR = A | B;  // OR_Gate or_1, 32 bits wide
  Comparator #(.width(32)) comparator_1 (.a(A), .b(B), .lt(comparator_1_lt));  // open: gt, eq
  Shifter #(.width(32)) shifter_1 (.in(A), .\dist (B[4:0]), .out(L_LEFT));
  Shifter #(.shift("lr"), .width(32)) shifter_2 (.in(A), .\dist (B[4:0]), .out(L_RIGHT));
  Clock clock_1 (.out(CLK));
  assign Comp_sig = {{31{comparator_1_lt}}, comparator_1_lt};  // Bit_Extender bit_extender_1
  Multiplexer #(.select(3), .width(32)) multiplexer_1 (
    .in0(ADD), .in1(REST), .in2(ALU_AND), .in3(ALU_OR), .in4(Comp_sig), .in5(L_LEFT), .in6(L_RIGHT), .in7(B),
    .out(RESULT), .sel(ALU_OP));
  Comparator #(.width(32)) comparator_2 (.a({32{1'b0}}), .b(RESULT), .eq(ZERO_F));  // open: gt, lt

  // Other names for the same wires on the sheet: ZERO = ZERO_F

  // Notes on the sheet:
  //   INPUTS
  //   OUTPUTS
endmodule
